# Fritzing sketch Curso_Programacion-Montaje Wemos0.1 (saved by Fritzing 0.9.3b)
breadboards: 1

parts:
  WeMos_D1_Mini1 = WeMos D1 Mini
  S1 = Pushbutton [package="[THT]"]

nets:
  N1: WeMos_D1_Mini1.3V3, S1.Pin_3, S1.Pin_4
  N2: WeMos_D1_Mini1.D3, S1.Pin_1, S1.Pin_2
